# Fritzing sketch BurglarAlarm (saved by Fritzing 0.9.3b)
breadboards: 1

parts:
  Part1 = Arduino Uno (Rev3)
  hc-sr1 = hc-sr04
  J1 = Piezo Speaker
  U1 = POT [package=alps_pot]
  U2 = LCD-16X2 [package=lcd-16x2]

nets:
  N1: Part1.D8, U2.E
  N2: Part1.D9_PWM, U2.DB4
  N3: Part1.D10_PWM/SS, U2.DB5
  N4: Part1.D11_PWM/MOSI, U2.DB6
  N5: Part1.D12/MISO, U2.DB7
  N6: Part1.D2, hc-sr1.Trig
  N7: Part1.D3_PWM, hc-sr1.Echo
  N8: Part1.D6_PWM, J1.pin2
  N9: Part1.D7, U2.RS
  N10: Part1.3V3, U2.A
  5V: Part1.5V, hc-sr1.VCC, U1.E, U2.VDD
  GND: Part1.GND, hc-sr1.GND, J1.pin1, U1.A, U2.VSS, U2.R_W, U2.K
  N11: U1.S, U2.VO
