# Fritzing sketch MemoryGameFr (saved by Fritzing 0.9.3b)
breadboards: 1

parts:
  S1 = Pushbutton [package="[THT]"]
  S2 = Pushbutton [package="[THT]"]
  S3 = Pushbutton [package="[THT]"]
  R1 = Resistor [tolerance=±5% resistance=220 package=THT]
  R2 = Resistor [tolerance=±5% resistance=220 package=THT]
  R3 = Resistor [tolerance=±5% resistance=220 package=THT]
  LED1 = LED - 3mm [color="Yellow (595nm)" package="3 mm [THT]"]
  LED2 = LED - 3mm [color="Red (633nm)" package="3 mm [THT]"]
  LED3 = LED - 3mm [color="Green (555nm)" package="3 mm [THT]"]
  J1 = Piezo Speaker
  R4 = Resistor [tolerance=±5% resistance=1k package=THT]
  R5 = Resistor [tolerance=±5% resistance=1k package=THT]
  R6 = Resistor [tolerance=±5% resistance=1k package=THT]
  Part1 = Arduino Uno (Rev3)

nets:
  N1: S1.Pin_1, S1.Pin_2, R6.Pin_0, Part1.D8
  N2: S1.Pin_3, S1.Pin_4, S2.Pin_3, S2.Pin_4, S3.Pin_3, S3.Pin_4, Part1.5V
  N3: S2.Pin_1, S2.Pin_2, R5.Pin_0, Part1.D9_PWM
  N4: S3.Pin_1, S3.Pin_2, R4.Pin_0, Part1.D10_PWM/SS
  N5: R1.Pin_0, R2.Pin_0, R3.Pin_0, J1.pin1, R4.Pin_1, R5.Pin_1, R6.Pin_1, Part1.GND
  N6: R1.Pin_1, LED1.anode
  N7: R2.Pin_1, LED2.anode
  N8: R3.Pin_1, LED3.anode
  N9: LED1.cathode, Part1.D4
  N10: LED2.cathode, Part1.D3_PWM
  N11: LED3.cathode, Part1.D2
  N12: J1.pin2, Part1.D7
